// Logisim project cpu.circ as structural Verilog: 2 circuits, main circuit main
module main (
  input  [31:0] INSTRUCTION,
  input  CLOCK,
  output [31:0] FETCH_ADDRESS,
  output [31:0] s0_Value,
  output [31:0] s1_Value,
  output [31:0] s2_Value,
  output [31:0] ra_Value,
  output [31:0] HI_Value,
  output [31:0] LO_Value
);

  wire MEM_p2, MEM_p7, MEM_p10, MEM_p14, MEM_p17, MEM_p20;
  wire [4:0] writeregister;
  wire [31:0] extend, main_1_read_data_1, main_1_read_data_2, main_2_result, MEM_p11, multiplexer_2_out,
       writedata;

  Register #(.width(32)) PC (.Q(FETCH_ADDRESS), .clk(CLOCK));  // open: D, en, clr
  Register #(.width(32)) LO ();  // open: D, en, Q, clk, clr
  Register #(.width(32)) HI ();  // open: D, en, Q, clk, clr
  assign extend = {{16{1'b0}}, INSTRUCTION[15:0]};  // Bit_Extender bit_extender_1
  regfile_main main_1 (
    .Read_Register_1(INSTRUCTION[25:21]), .Read_Register_2(INSTRUCTION[20:16]),
    .Write_Register(writeregister), .Write_Data(writedata), .Read_Data_1(main_1_read_data_1),
    .Read_Data_2(main_1_read_data_2));  // open: Write_Enable, Clock, s0_Value, s1_Value, s2_Value, ra_Value, in_5
  Multiplexer #(.width(5)) multiplexer_1 (
    .in0(INSTRUCTION[20:16]), .in1(INSTRUCTION[15:11]), .out(writeregister));  // open: sel, en
  Multiplexer #(.width(32)) multiplexer_2 (
    .in0(main_1_read_data_2), .in1(extend), .out(multiplexer_2_out));  // open: sel, en
  alu_main main_2 (
    .X(main_1_read_data_1), .Result(main_2_result), .Y(multiplexer_2_out));  // open: Switch, Equal, Signed_Overflow, Result_2
  // mem_main MEM: pin names not known; wires that end beside it: s0_Value, MEM_p2, MEM_p2, s1_Value, main_2_result, main_1_read_data_2, MEM_p7, MEM_p7, s2_Value, MEM_p10, MEM_p11, MEM_p10, ra_Value, MEM_p14, MEM_p14, HI_Value, MEM_p17, MEM_p17, LO_Value, MEM_p20
  Multiplexer #(.width(32)) multiplexer_3 (.in0(main_2_result), .in1(MEM_p11), .out(writedata));  // open: sel, en

  // Other names for the same wires on the sheet: clk = CLOCK; fetch_addr[31:0] = FETCH_ADDRESS;
  //   readregister2[4:0] = INSTRUCTION[20:16]; readregister1[4:0] = INSTRUCTION[25:21]

  // Notes on the sheet:
  //   Output
  //   These are outputs/inputs from run.circ
  //   Inputs
  //   These are DEBUG/TEST outputs from your circuit.
endmodule

module maincontrol (
  input  [5:0] instruction,
  input  [9:0] addiu,
  input  [9:0] addi,
  input  [9:0] sb,
  input  [9:0] bne,
  input  [9:0] lhu,
  input  [9:0] beq,
  input  [9:0] lbu,
  input  [9:0] lb,
  input  [9:0] R_Type,
  input  [9:0] jal,
  input  [9:0] lw,
  input  [9:0] andi,
  input  [9:0] swinc,
  input  [9:0] sh,
  input  [9:0] j___jal,
  input  [9:0] lui,
  input  [9:0] ori,
  input  [9:0] sw,
  input  [9:0] slti,
  output RegDst,
  output Jump,
  output Branch,
  output MemRead,
  output MemToReg,
  output [1:0] ALUOP,
  output MemWrite,
  output ALUSrc,
  output RegWrite
);

  wire [9:0] andi_t, jal_t, lui_t, lw_t, multiplexer_1_out, multiplexer_2_out, ori_t, sh_t, slti_t, sw_t,
       swinc_t;

  Multiplexer #(.select(5), .width(10)) multiplexer_1 (
    .in0(R_Type), .in2(jal_t), .in3(jal_t), .in5(bne), .in8(addi), .in9(addiu), .in10(slti_t), .in11(sw_t),
    .in12(andi_t), .in13(ori_t), .in15(lui_t), .out(multiplexer_1_out), .sel(instruction[4:0]));  // open: in1, in4, in6, in7, in14, in16, in17, in18, in19, in20, in21, in22, in23, in24, in25, in26, in27, in28, in29, in30, in31, en
  Multiplexer #(.select(5), .width(10)) multiplexer_2 (
    .in0(lb), .in3(lw_t), .in5(lhu), .in8(sb), .in9(sh_t), .in10(slti_t), .in11(sw_t), .in12(swinc_t),
    .in13(ori_t), .in15(lui_t), .out(multiplexer_2_out), .sel(instruction[4:0]));  // open: in1, in2, in4, in6, in7, in14, in16, in17, in18, in19, in20, in21, in22, in23, in24, in25, in26, in27, in28, in29, in30, in31, en
  Multiplexer #(.width(10)) multiplexer_3 (
    .in0(multiplexer_1_out), .in1(multiplexer_2_out),
    .out({RegWrite, ALUSrc, MemWrite, ALUOP, MemToReg, MemRead, Branch, Jump, RegDst}), .sel(instruction[5]));  // open: en

  // Other names for the same wires on the sheet: mux1[4:0] = instruction[4:0]; rtype[9:0] = R_Type
endmodule
